// Logisim project A1_Group4.circ as structural Verilog: 3 circuits, main circuit ALU
module ALU (
  input  _3,
  input  _2,
  input  _1,
  input  B,
  input  _3_2,
  input  _2_2,
  input  _1_2,
  input  A,
  input  _3_3,
  input  _2_3,
  input  _1_3,
  output _4,
  output _3_4,
  output _2_4,
  output _1_4,
  output V,
  output C,
  output Z,
  output S
);

  wire n7408_1_p3, n7408_1_p6, n7408_1_p11, n7408_1_p12, n7408_1_p13, n7408_2_p3, n7408_2_p4, n7408_2_p6,
       n7408_2_p10, n7408_2_p13, n7408_2_p14, n7432_1_p2, n7432_1_p5, n7432_1_p6, n7432_1_p11, n7486_1_p1,
       n7486_1_p8, n7486_1_p11, n74157_1_p4, n74157_1_p7, n74157_1_p13, n74157_1_p16;

  // _7486 7486_1: pin names not known; wires that end beside it: n7486_1_p1, C, V, 1'b0, 1'b1, 1'b1, _3, n7486_1_p8, _3, _1, n7486_1_p11
  // _7408 7408_1: pin names not known; wires that end beside it: _1, _2, n7408_1_p3, n7408_1_p3, n7486_1_p8, n7408_1_p6, 1'b0, 1'b1, _3, _2, n7408_1_p11, n7408_1_p12, n7408_1_p13, C
  // _7432 7432_1: pin names not known; wires that end beside it: n7486_1_p8, n7432_1_p2, n7408_1_p13, _4, n7432_1_p5, n7432_1_p6, 1'b0, 1'b1, n7486_1_p11, n7408_1_p11, n7432_1_p11, _1_4, _2_4, n7432_1_p5
  // _7402 7402_1: pin names not known; wires that end beside it: n7432_1_p2, _2, _1, Z, n7432_1_p6, _3_4, 1'b0, 1'b1
  // _74157 74157_1: pin names not known; wires that end beside it: n7432_1_p11, 1'b1, _1_2, n74157_1_p4, 1'b1, _2_2, n74157_1_p7, 1'b0, 1'b1, n7408_1_p6, 1'b1, B, n74157_1_p13, 1'b1, _3_2, n74157_1_p16
  // _7408 7408_2: pin names not known; wires that end beside it: _3, n7408_1_p13, n7408_2_p3, n7408_2_p4, n7408_1_p13, n7408_2_p6, 1'b0, 1'b1, n7408_1_p13, n7408_2_p10, n7486_1_p1, n7408_1_p13, n7408_2_p13, n7408_2_p14
  _7483 u_7483_1 (
    .A4(n74157_1_p13), .A3(n7486_1_p1), .B3(1'b1), .Vcc(1'b1), .S2(n7408_2_p10), .B2(1'b0), .A2(1'b0),
    .B4(A), .S4(_4), .Cout(n7408_1_p12), .Cin(n7408_2_p14), .GND(1'b0), .B1(_3_3), .A1(n74157_1_p16),
    .S1(_3_4));  // open: S3
  _7483 u_7483_2 (
    .A4(n74157_1_p7), .A3(n7408_2_p6), .B3(1'b1), .Vcc(1'b1), .S2(n7408_2_p4), .B2(1'b0), .A2(1'b0),
    .B4(_2_3), .S4(_2_4), .Cout(n7408_2_p13), .Cin(n7408_2_p3), .GND(1'b0), .B1(_1_3), .A1(n74157_1_p4),
    .S1(_1_4));  // open: S3

  assign S = _4;

  // Notes on the sheet:
  //   4
  //   4
endmodule

module _7483 (
  input  A4,
  input  B4,
  input  A3,
  input  B3,
  input  Cin,
  input  Vcc,
  input  GND,
  input  B1,
  input  B2,
  input  A1,
  input  A2,
  output S3,
  output S4,
  output Cout,
  output S2,
  output S1
);

  wire and_1_out, and_2_out, and_3_out, and_4_out, and_5_out, and_6_out, and_7_out, and_8_out, and_9_out,
       and_10_out, and_11_out, and_12_out, and_13_out, and_14_out, nand_1_out, nand_2_out, nand_3_out,
       nand_4_out, nor_1_out, nor_2_out, nor_3_out, nor_4_out, nor_6_out, nor_7_out, nor_8_out, not_1_out,
       not_2_out, not_3_out, not_4_out, not_5_out, not_6_out;

  nand nand_1 (nand_1_out, B4, A4);
  nor nor_1 (nor_1_out, B4, A4);
  nand nand_2 (nand_2_out, B3, A3);
  nor nor_2 (nor_2_out, B3, A3);
  nand nand_3 (nand_3_out, B2, A2);
  nor nor_3 (nor_3_out, B2, A2);
  nand nand_4 (nand_4_out, B1, A1);
  nor nor_4 (nor_4_out, B1, A1);
  and and_1 (and_1_out, nor_2_out, nand_1_out);
  and and_2 (and_2_out, nor_3_out, nand_1_out, nand_2_out);
  and and_3 (and_3_out, nor_4_out, nand_1_out, nand_2_out, nand_3_out);
  and and_4 (and_4_out, nand_1_out, nand_2_out, nand_3_out, nand_4_out, not_2_out);
  and and_5 (and_5_out, nand_1_out, not_1_out);
  not not_1 (not_1_out, nor_1_out);
  and and_6 (and_6_out, nor_3_out, nand_2_out);
  and and_7 (and_7_out, nor_4_out, nand_2_out, nand_3_out);
  and and_8 (and_8_out, nand_2_out, nand_3_out, nand_4_out, not_2_out);
  not not_2 (not_2_out, Cin);
  and and_9 (and_9_out, nand_2_out, not_3_out);
  not not_3 (not_3_out, nor_2_out);
  and and_10 (and_10_out, nor_4_out, nand_3_out);
  and and_11 (and_11_out, nand_3_out, nand_4_out, not_2_out);
  and and_12 (and_12_out, nand_3_out, not_4_out);
  not not_4 (not_4_out, nor_3_out);
  and and_13 (and_13_out, nand_4_out, not_2_out);
  and and_14 (and_14_out, nand_4_out, not_5_out);
  not not_5 (not_5_out, nor_4_out);
  not not_6 (not_6_out, not_2_out);
  nor nor_5 (Cout, nor_1_out, and_1_out, and_2_out, and_3_out, and_4_out);
  nor nor_6 (nor_6_out, nor_2_out, and_6_out, and_7_out, and_8_out);
  nor nor_7 (nor_7_out, nor_3_out, and_10_out, and_11_out);
  nor nor_8 (nor_8_out, nor_4_out, and_13_out);
  xor xor_1 (S4, and_5_out, nor_6_out);
  xor xor_2 (S3, and_9_out, nor_7_out);
  xor xor_3 (S2, and_12_out, nor_8_out);
  xor xor_4 (S1, and_14_out, not_6_out);
endmodule

module Main (
  input  A3,
  input  A2,
  input  A1,
  input  A0,
  input  B3,
  input  B2,
  input  B1,
  input  B0,
  input  cs2,
  input  cs1,
  input  cs0,
  output S3,
  output S2,
  output S1,
  output S0,
  output Z,
  output V,
  output S,
  output Cout
);

  ALU alu_1 (
    ._4(S3), ._3_4(S2), ._2_4(S1), ._1_4(S0), ._3(cs2), ._2(cs1), .B(B3), ._3_2(B2), ._2_2(B1), ._1_2(B0),
    .Z(Z), .V(V), .S(S), .C(Cout), .A(A3), ._3_3(A2), ._2_3(A1), ._1_3(A0), ._1(cs0));
endmodule
